# Fritzing sketch Clapping_lamp_fritzing (saved by Fritzing 0.9.3b)
breadboards: 1

parts:
  Part1 = Arduino Uno (Rev3)
  Q1 = TRANSISTOR_NPN [package=to-92]
  FC-1 = Sound Sensor
  U1 = WS2812 RGB LED strip
  Power1 = PowerBRICK 12V

nets:
  N1: Part1.D9_PWM, Q1.B
  N2: Part1.D7, FC-1.OUT
  5V: Part1.5V, FC-1.VCC
  GND: Part1.GND, Q1.C, FC-1.GND, Power1.GND
  N3: Q1.E, U1.VCC
  N4: U1.GND, Power1.-Vout

custom parts:
  WS2812 RGB LED strip: WS2812 strip
  PowerBRICK 12V: PowerBRICKs are split-rail power supply modules that are intended to be used with a breadboard. These generate both a negative and positive voltage out of a single 5V USB voltage.
